// Digital circuit 8-bit-Processor.dig as structural Verilog
module _8_bit_Processor (
  input  [7:0] InstrMem_Input,
  input  [1:0] InstrMem_ctrl,
  input  clk,
  output [7:0] IR_Output,
  output Inst_Fetch,
  output Instr_Decode,
  output Instr_Exec,
  output Write_Back,
  output [1:0] IR_CTRL,
  output [2:0] Program_Counter,
  output [7:0] RegFile_ctrl,
  output [7:0] ALU_Output
);

  wire [7:0] _8_bit_memory_1_output, multiplexer_1_out, multiplexer_3_out, registerfile_1_read_data1,
       registerfile_1_read_data2;
  wire [7:3] pc_1_p4;

  // PC pc_1: pin names not known; wires that end beside it: {1'b0, Write_Back}, 2'b01, clk, {pc_1_p4, Program_Counter}
  _8_bit_memory _8_bit_memory_1 (
    .Address_pin(Program_Counter), .Data_input(InstrMem_Input), .CLK(clk), .CTRL(InstrMem_ctrl),
    .Output(_8_bit_memory_1_output));
  // control_unit control_unit_1: pin names not known; wires that end beside it: clk, Inst_Fetch, Instr_Decode, Instr_Exec, Write_Back
  // IR ir_1: pin names not known; wires that end beside it: _8_bit_memory_1_output, {1'b0, Inst_Fetch}, clk, IR_Output
  Multiplexer #(.Selector_Bits(2), .Bits(8)) multiplexer_1 (
    .sel(IR_Output[4:3]), .in_0(8'h1), .in_1(8'h4), .in_2(8'h10), .in_3(8'h40), .out(multiplexer_1_out));
  Multiplexer #(.Bits(8)) multiplexer_2 (
    .sel(Instr_Decode), .in_0({8{1'b0}}), .in_1(multiplexer_1_out), .out(RegFile_ctrl));
  registerfile registerfile_1 (
    .clk(clk), .Read_Register1(IR_Output[4:3]), .Read_Register2(IR_Output[2:1]), .Write_Data(ALU_Output),
    .Write_Register(IR_Output[4:3]), .ctrl(RegFile_ctrl), .Read_Data1(registerfile_1_read_data1),
    .Read_Data2(registerfile_1_read_data2));
  Multiplexer #(.Bits(8)) multiplexer_3 (
    .sel(IR_Output[0]), .in_0(registerfile_1_read_data1), .in_1({{6{1'b0}}, IR_Output[2:1]}),
    .out(multiplexer_3_out));
  // ALU alu_1: pin names not known; wires that end beside it: multiplexer_3_out, IR_Output[7:5], registerfile_1_read_data2, ALU_Output

  assign IR_CTRL = {1'b0, Inst_Fetch};
endmodule
