// Digital circuit 8-bit-full-adder.dig as structural Verilog
module _8_bit_full_adder (
  input  [7:0] A,
  input  [7:0] Y,
  input  Carry_in,
  output Carry_out,
  output [7:0] Sum
);

  wire add_1_s, add_2_c_o, add_2_s, add_3_c_o, add_3_s, add_4_c_o, add_4_s, add_5_c_o, add_5_s, add_6_c_o,
       add_6_s, add_7_c_o, add_7_s, add_8_c_o;
  wire [7:1] undriven;

  Add add_1 (.a(A[7]), .b(Y[7]), .c_i(add_2_c_o), .s(add_1_s), .c_o(Carry_out));
  Add add_2 (.a(A[6]), .b(Y[6]), .c_i(add_3_c_o), .s(add_2_s), .c_o(add_2_c_o));
  Add add_3 (.a(A[5]), .b(Y[5]), .c_i(add_4_c_o), .s(add_3_s), .c_o(add_3_c_o));
  Add add_4 (.a(A[4]), .b(Y[4]), .c_i(add_5_c_o), .s(add_4_s), .c_o(add_4_c_o));
  Add add_5 (.a(A[3]), .b(Y[3]), .c_i(add_6_c_o), .s(add_5_s), .c_o(add_5_c_o));
  Add add_6 (.a(A[2]), .b(Y[2]), .c_i(add_7_c_o), .s(add_6_s), .c_o(add_6_c_o));
  Add add_7 (.a(A[1]), .b(Y[1]), .c_i(add_8_c_o), .s(add_7_s), .c_o(add_7_c_o));
  Add add_8 (.a(A[0]), .b(Y[0]), .c_i(Carry_in), .s(Sum[0]), .c_o(add_8_c_o));
  // Pins of 1 and 8 bits meet at {undriven, Sum[0]}
  // Pins of 1 and 8 bits meet at Sum
endmodule
