// Digital circuit 8-bit-memory.dig as structural Verilog
module _8_bit_memory (
  input  [2:0] Address_pin,
  input  [7:0] Data_input,
  input  [7:0] CLK,
  input  [1:0] CTRL,
  output [7:0] Output
);

  wire and_2_out, and_3_out, and_4_out, and_5_out, and_6_out, and_7_out, and_8_out, demultiplexer_1_out_1,
       demultiplexer_1_out_2, demultiplexer_1_out_3, demultiplexer_1_out_4, demultiplexer_1_out_5,
       demultiplexer_1_out_6, demultiplexer_1_out_7;
  wire [7:0] _8_bit_register_1_p4, _8_bit_register_2_p4, _8_bit_register_3_p4, _8_bit_register_4_p4,
       _8_bit_register_5_p4, _8_bit_register_6_p4, _8_bit_register_7_p4, _8_bit_register_8_p4, and_1_out,
       demultiplexer_1_out_0;

  Demultiplexer #(.Selector_Bits(3)) demultiplexer_1 (
    .sel(Address_pin), .out_0(demultiplexer_1_out_0[0]), .out_1(demultiplexer_1_out_1),
    .out_2(demultiplexer_1_out_2), .out_3(demultiplexer_1_out_3), .out_4(demultiplexer_1_out_4),
    .out_5(demultiplexer_1_out_5), .out_6(demultiplexer_1_out_6), .out_7(demultiplexer_1_out_7));  // open: in
  assign and_1_out = CLK & demultiplexer_1_out_0;  // And and_1, 8 bits wide
  and and_2 (and_2_out, CLK[0], demultiplexer_1_out_1);
  and and_3 (and_3_out, CLK[0], demultiplexer_1_out_2);
  and and_4 (and_4_out, CLK[0], demultiplexer_1_out_3);
  and and_5 (and_5_out, CLK[0], demultiplexer_1_out_4);
  and and_6 (and_6_out, CLK[0], demultiplexer_1_out_5);
  and and_7 (and_7_out, CLK[0], demultiplexer_1_out_6);
  and and_8 (and_8_out, CLK[0], demultiplexer_1_out_7);
  // _8_bit_register _8_bit_register_1: pin names not known; wires that end beside it: and_1_out, Data_input, CTRL, _8_bit_register_1_p4
  // _8_bit_register _8_bit_register_2: pin names not known; wires that end beside it: and_2_out, Data_input, CTRL, _8_bit_register_2_p4
  // _8_bit_register _8_bit_register_3: pin names not known; wires that end beside it: and_3_out, Data_input, CTRL, _8_bit_register_3_p4
  // _8_bit_register _8_bit_register_4: pin names not known; wires that end beside it: and_4_out, Data_input, CTRL, _8_bit_register_4_p4
  // _8_bit_register _8_bit_register_5: pin names not known; wires that end beside it: and_5_out, Data_input, CTRL, _8_bit_register_5_p4
  // _8_bit_register _8_bit_register_6: pin names not known; wires that end beside it: and_6_out, Data_input, CTRL, _8_bit_register_6_p4
  // _8_bit_register _8_bit_register_7: pin names not known; wires that end beside it: and_7_out, Data_input, CTRL, _8_bit_register_7_p4
  // _8_bit_register _8_bit_register_8: pin names not known; wires that end beside it: and_8_out, Data_input, CTRL, _8_bit_register_8_p4
  Multiplexer #(.Bits(8), .Selector_Bits(3)) multiplexer_1 (
    .sel(Address_pin), .in_0(_8_bit_register_1_p4), .in_1(_8_bit_register_2_p4), .in_2(_8_bit_register_3_p4),
    .in_3(_8_bit_register_4_p4), .in_4(_8_bit_register_5_p4), .in_5(_8_bit_register_6_p4),
    .in_6(_8_bit_register_7_p4), .in_7(_8_bit_register_8_p4), .out(Output));
  // Pins of 1 and 8 bits meet at CLK
  // Pins of 1 and 8 bits meet at demultiplexer_1_out_0
endmodule
