// Digital circuit PC.dig as structural Verilog
module PC (
  input  [7:0] Carry,
  input  [1:0] CTRL,
  input  CLK,
  output [7:0] Output
);

  wire [7:0] _8_bit_full_adder_1_sum;
  wire [7:1] multiplexer_1_out;

  _8_bit_full_adder _8_bit_full_adder_1 (
    .A(Output), .Y(Carry), .Carry_in(1'b0), .Sum(_8_bit_full_adder_1_sum));  // open: Carry_out
  Multiplexer #(.Selector_Bits(2), .Bits(8)) multiplexer_1 (
    .sel(CTRL), .in_0(Output), .in_1(_8_bit_full_adder_1_sum), .in_2({8{1'b0}}), .in_3({8{1'b1}}),
    .out({multiplexer_1_out, Output[1]}));
  D_FF d_ff_1 (.D(multiplexer_1_out[7]), .C(CLK), .Q(Output[7]));  // open: nQ
  D_FF d_ff_2 (.D(multiplexer_1_out[6]), .C(CLK), .Q(Output[6]));  // open: nQ
  D_FF d_ff_3 (.D(multiplexer_1_out[5]), .C(CLK), .Q(Output[5]));  // open: nQ
  D_FF d_ff_4 (.D(multiplexer_1_out[4]), .C(CLK), .Q(Output[4]));  // open: nQ
  D_FF d_ff_5 (.D(multiplexer_1_out[3]), .C(CLK), .Q(Output[3]));  // open: nQ
  D_FF d_ff_6 (.D(multiplexer_1_out[2]), .C(CLK), .Q(Output[2]));  // open: nQ
  D_FF d_ff_7 (.D(multiplexer_1_out[1]), .C(CLK), .Q(Output[1]));  // open: nQ
  D_FF d_ff_8 (.D(Output[1]), .C(CLK), .Q(Output[0]));  // open: nQ
endmodule
