// Digital circuit Registers_SRAM.dig as structural Verilog
module Registers_SRAM (
  input  [3:0] Address,
  input  CS,
  input  WE,
  input  OE,
  input  IR_sel,
  input  LD,
  input  CLK,
  input  [7:0] Alt_input,
  input  [7:0] Data_in,
  output [7:0] Output
);

  RAMSinglePortSel #(.AddrBits(4), .Bits(8)) ramsingleportsel_1 (.A(Address), .CS(CS), .WE(WE), .OE(OE), .D(Data_in));
  // IR ir_1: pin names not known; wires that end beside it: Data_in, CLK, Alt_input, IR_sel, LD, Output
endmodule
