// Digital circuit register_file_ALU.dig as structural Verilog
module register_file_ALU (
  input  clk,
  input  [1:0] Read_Register1,
  input  [1:0] Read_Register2,
  input  [1:0] Write_Register,
  input  [7:0] ctrl,
  input  [2:0] Opcode,
  input  [7:0] Write_Data,
  input  Write_Select
);

  wire [7:0] alu_1_p4, multiplexer_1_out, registerfile_1_read_data1, registerfile_1_read_data2;

  Multiplexer #(.Bits(8)) multiplexer_1 (
    .sel(Write_Select), .in_0(Write_Data), .in_1(alu_1_p4), .out(multiplexer_1_out));
  registerfile registerfile_1 (
    .clk(clk), .Read_Register1(Read_Register1), .Read_Register2(Read_Register2),
    .Write_Data(multiplexer_1_out), .Write_Register(Write_Register), .ctrl(ctrl),
    .Read_Data1(registerfile_1_read_data1), .Read_Data2(registerfile_1_read_data2));
  // ALU alu_1: pin names not known; wires that end beside it: registerfile_1_read_data1, Opcode, registerfile_1_read_data2, alu_1_p4
endmodule
