// Digital circuit registerfile.dig as structural Verilog
module registerfile (
  input  clk,
  input  [1:0] Read_Register1,
  input  [1:0] Read_Register2,
  input  [7:0] Write_Data,
  input  [1:0] Write_Register,
  input  [7:0] ctrl,
  output [7:0] Read_Data1,
  output [7:0] Read_Data2
);

  wire [7:0] _8_bit_register_1_p4, _8_bit_register_2_p4, _8_bit_register_3_p4, _8_bit_register_4_p4,
       demultiplexer_1_out_0, demultiplexer_1_out_1, demultiplexer_1_out_2, demultiplexer_1_out_3;

  Demultiplexer #(.Selector_Bits(2), .Bits(8)) demultiplexer_1 (
    .sel(Write_Register), .in(Write_Data), .out_0(demultiplexer_1_out_0), .out_1(demultiplexer_1_out_1),
    .out_2(demultiplexer_1_out_2), .out_3(demultiplexer_1_out_3));
  // _8_bit_register _8_bit_register_1: pin names not known; wires that end beside it: clk, demultiplexer_1_out_0, ctrl[1:0], _8_bit_register_1_p4
  // _8_bit_register _8_bit_register_2: pin names not known; wires that end beside it: clk, demultiplexer_1_out_1, ctrl[3:2], _8_bit_register_2_p4
  // _8_bit_register _8_bit_register_3: pin names not known; wires that end beside it: clk, demultiplexer_1_out_2, ctrl[5:4], _8_bit_register_3_p4
  // _8_bit_register _8_bit_register_4: pin names not known; wires that end beside it: clk, demultiplexer_1_out_3, ctrl[7:6], _8_bit_register_4_p4
  Multiplexer #(.Selector_Bits(2), .Bits(8)) multiplexer_1 (
    .sel(Read_Register1), .in_0(_8_bit_register_1_p4), .in_1(_8_bit_register_2_p4),
    .in_2(_8_bit_register_3_p4), .in_3(_8_bit_register_4_p4), .out(Read_Data1));
  Multiplexer #(.Selector_Bits(2), .Bits(8)) multiplexer_2 (
    .sel(Read_Register2), .in_0(_8_bit_register_4_p4), .in_1(_8_bit_register_3_p4),
    .in_2(_8_bit_register_2_p4), .in_3(_8_bit_register_1_p4), .out(Read_Data2));

  // Notes on the sheet:
  //   clk: Hz: 2
endmodule
